// Logisim project ConvertByteWord.circ as structural Verilog: 1 circuit, main circuit CBW
module CBW (
  input  [7:0] R0,
  input  Cin,
  input  Oin,
  output [7:0] ACC,
  output [7:0] ACC2,
  output C,
  output O,
  output S,
  output Z
);

  Comparator comparator_1 (.a(R0), .b({8{1'b0}}), .eq(Z));  // open: gt, lt

  assign ACC = R0;
  assign ACC2 = {8{R0[7]}};
  assign C = Cin;
  assign O = Oin;
  assign S = R0[7];
endmodule
